# Fritzing sketch sketch (saved by Fritzing 1.0.1rc)
breadboards: 1

parts:
  P1 = S1133 Si Photodiode [package="8mm Ceramic [THT]"]
  P2 = S1133 Si Photodiode [package="8mm Ceramic [THT]"]
  P3 = S1133 Si Photodiode [package="8mm Ceramic [THT]"]
  P4 = S1133 Si Photodiode [package="8mm Ceramic [THT]"]
  IC1 = LM324 [package=dil16]
  U1 = ESP32S-HiLetgo [part_number=ESP32S-HiLetgo]
  R1 = Resistor [tolerance=±5% resistance=100k package="0603 [SMD]"]
  R2 = Resistor [tolerance=±5% resistance=100k package="0603 [SMD]"]
  R3 = Resistor [tolerance=±5% resistance=100k package="0603 [SMD]"]
  R4 = Resistor [tolerance=±5% resistance=100k package="0603 [SMD]"]
  Part1 = Adafruit ICM20948

nets:
  GND: P1.cathode, P2.cathode, P3.cathode, P4.cathode, IC1.IN1+, IC1.IN2+, IC1.IN3+, IC1.GND, IC1.IN4+, U1.GND, Part1.GND
  N1: P1.anode, IC1.IN1-, R2.Pin_1
  N2: P2.anode, IC1.IN4-, R1.Pin_0
  N3: P3.anode, IC1.IN3-, R3.Pin_1
  N4: P4.anode, IC1.IN2-, R4.Pin_0
  N5: IC1.OUT1, U1.GPIO34, R2.Pin_0
  N6: IC1.V+, U1.VIN
  N7: IC1.OUT2, U1.GPIO35, R4.Pin_1
  N8: IC1.OUT3, U1.GPIO33, R3.Pin_0
  N9: IC1.OUT4, U1.GPIO32, R1.Pin_1
  N10: U1.3.3, Part1.VIN
  N11: U1.GPIO1, Part1.SDI/SDA
  N12: U1.GPIO22, Part1.SCK/SCL

custom parts:
  LM324: LM324 Quad OpAmp
  ESP32S-HiLetgo: HiLetgo ESP-WROOM-32 ESP32 ESP-32S Development Board 2.4GHz Dual-Mode WiFi + Bluetooth Dual Cores Microcontroller The ESP32 integrated with Antenna switches, RF Balun, power amplifiers, low-noise amplifiers, filters, and management modules, and the entire solution occupies the least area of PCB. 2.4 GHz Wi-Fi plus Bluetooth dual-mode chip, with TSMC Ultra-low power consumption 40nm technology,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
